# Fritzing sketch esquema_ligacoes (saved by Fritzing 0.9.10b)
breadboards: 1

parts:
  U1 = ESP32S-HiLetgo [part_number=ESP32S-HiLetgo]
  IR1 = TSOP312.., 314.. [package=THT]
  R1 = Resistor [tolerance=±5% resistance=220 package="0805 [SMD]"]
  LED2 = smd LED [color="Infrared (850nm)" current=0A package="0805 [SMD]"]
  R2 = Resistor [tolerance=±5% resistance=220 package="0805 [SMD]"]
  LED3 = smd LED [color="Red (633nm)" current=0A package="0805 [SMD]"]

nets:
  N1: U1.GND, R1.Pin_1, R2.Pin_1
  N2: U1.GPIO11, IR1.GND, LED2.cathode, LED3.cathode
  N3: U1.VIN, IR1.Vs
  N4: U1.GPIO5, IR1.Data
  N5: R1.Pin_0, LED3.anode
  N6: LED2.anode, R2.Pin_0

custom parts:
  ESP32S-HiLetgo: HiLetgo ESP-WROOM-32 ESP32 ESP-32S Development Board 2.4GHz Dual-Mode WiFi + Bluetooth Dual Cores Microcontroller The ESP32 integrated with Antenna switches, RF Balun, power amplifiers, low-noise amplifiers, filters, and management modules, and the entire solution occupies the least area of PCB. 2.4 GHz Wi-Fi plus Bluetooth dual-mode chip, with TSMC Ultra-low power consumption 40nm technology,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
